// Logisim project alarme-residencial.circ as structural Verilog
module comparador_4bits (
  input  in_1,
  input  in_2,
  input  in_3,
  input  in_4,
  input  in_5,
  input  in_6,
  input  in_7,
  input  in_8,
  output out_9
);

  wire and_1_out, and_2_out, xnor_1_out, xnor_2_out, xnor_3_out, xnor_4_out;

  xnor xnor_1 (xnor_1_out, in_1, in_2);
  xnor xnor_2 (xnor_2_out, in_3, in_4);
  xnor xnor_3 (xnor_3_out, in_5, in_6);
  xnor xnor_4 (xnor_4_out, in_7, in_8);
  and and_1 (and_1_out, xnor_1_out, xnor_2_out);
  and and_2 (and_2_out, xnor_3_out, xnor_4_out);
  and and_3 (out_9, and_1_out, and_2_out);
endmodule

module entrada_senha (
  input  in_1,
  input  in_2,
  input  in_3,
  input  in_4,
  input  in_5,
  input  in_6,
  input  in_7,
  input  in_8,
  input  in_9,
  input  in_10,
  input  in_11,
  input  in_12,
  input  in_13,
  input  in_14,
  input  in_15,
  input  in_16,
  input  in_17,
  input  in_18,
  input  in_19,
  input  in_20,
  input  in_21,
  input  in_22,
  input  in_23,
  input  in_24,
  input  in_25,
  input  in_26,
  input  in_27,
  input  in_28,
  input  in_29,
  input  in_30,
  input  in_31,
  input  in_32,
  input  in_33,
  input  in_34,
  input  in_35,
  input  in_36,
  input  in_37,
  input  in_38,
  input  in_39,
  input  in_40,
  input  in_41,
  input  in_42,
  input  in_43,
  input  in_44,
  input  in_45,
  input  in_46,
  input  in_47,
  input  in_48,
  input  in_49,
  input  in_50,
  input  in_51,
  input  in_52,
  input  in_53,
  input  in_54,
  input  in_55,
  input  in_56,
  input  in_57,
  input  in_58,
  input  in_59,
  input  in_60,
  input  in_61,
  input  in_62,
  input  in_63,
  input  in_64,
  input  in_65,
  input  in_66,
  input  in_67,
  input  in_68,
  input  in_69,
  input  in_70,
  input  in_71,
  input  in_72,
  input  in_73,
  input  in_74,
  input  in_75,
  input  in_76,
  input  in_77,
  input  in_78,
  input  in_79,
  input  in_80,
  input  in_81,
  input  in_82,
  input  in_83,
  input  in_84,
  input  in_85,
  input  in_86,
  input  in_87,
  input  in_88,
  input  in_89,
  input  in_90,
  input  in_91,
  input  in_92,
  input  in_93,
  input  in_94,
  input  in_95,
  input  in_96,
  input  in_97,
  input  in_98,
  input  in_99,
  input  in_100,
  input  in_101,
  input  in_102,
  input  in_103,
  input  in_104,
  input  in_105,
  input  in_106,
  input  in_107,
  input  in_108,
  input  in_109,
  input  in_110,
  input  in_111,
  input  in_112,
  input  in_113,
  input  in_114,
  input  in_115,
  input  in_116,
  input  in_117,
  input  in_118,
  input  in_119,
  input  in_120,
  output out_121
);

  wire and_1_out, and_2_out, and_3_out, and_4_out, codificador_4bits_1_out_11, codificador_4bits_1_out_12,
       codificador_4bits_1_out_13, codificador_4bits_1_out_14, codificador_4bits_2_out_11,
       codificador_4bits_2_out_12, codificador_4bits_2_out_13, codificador_4bits_2_out_14,
       codificador_4bits_3_out_11, codificador_4bits_3_out_12, codificador_4bits_3_out_13,
       codificador_4bits_3_out_14, codificador_4bits_4_out_11, codificador_4bits_4_out_12,
       codificador_4bits_4_out_13, codificador_4bits_4_out_14, codificador_4bits_5_out_11,
       codificador_4bits_5_out_12, codificador_4bits_5_out_13, codificador_4bits_5_out_14,
       codificador_4bits_6_out_11, codificador_4bits_6_out_12, codificador_4bits_6_out_13,
       codificador_4bits_6_out_14, codificador_4bits_7_out_11, codificador_4bits_7_out_12,
       codificador_4bits_7_out_13, codificador_4bits_7_out_14, codificador_4bits_8_out_11,
       codificador_4bits_8_out_12, codificador_4bits_8_out_13, codificador_4bits_8_out_14,
       codificador_4bits_9_out_11, codificador_4bits_9_out_12, codificador_4bits_9_out_13,
       codificador_4bits_9_out_14, codificador_4bits_10_out_11, codificador_4bits_10_out_12,
       codificador_4bits_10_out_13, codificador_4bits_10_out_14, codificador_4bits_11_out_11,
       codificador_4bits_11_out_12, codificador_4bits_11_out_13, codificador_4bits_11_out_14,
       codificador_4bits_12_out_11, codificador_4bits_12_out_12, codificador_4bits_12_out_13,
       codificador_4bits_12_out_14, comparador_4bits_1_out_9, comparador_4bits_2_out_9,
       comparador_4bits_3_out_9, comparador_4bits_4_out_9, comparador_4bits_5_out_9, comparador_4bits_6_out_9;

  codificador_4bits codificador_4bits_1 (
    .in_1(in_4), .in_2(in_9), .in_3(in_14), .in_4(in_19), .in_5(in_24), .in_6(in_30), .in_7(in_36),
    .in_8(in_42), .in_9(in_48), .in_10(in_54), .out_11(codificador_4bits_1_out_11),
    .out_12(codificador_4bits_1_out_12), .out_13(codificador_4bits_1_out_13),
    .out_14(codificador_4bits_1_out_14));
  codificador_4bits codificador_4bits_2 (
    .in_1(in_61), .in_2(in_63), .in_3(in_65), .in_4(in_67), .in_5(in_72), .in_6(in_78), .in_7(in_84),
    .in_8(in_90), .in_9(in_96), .in_10(in_102), .out_11(codificador_4bits_2_out_11),
    .out_12(codificador_4bits_2_out_12), .out_13(codificador_4bits_2_out_13),
    .out_14(codificador_4bits_2_out_14));
  comparador_4bits comparador_4bits_1 (
    .in_1(codificador_4bits_1_out_11), .in_2(codificador_4bits_2_out_11), .in_3(codificador_4bits_1_out_12),
    .in_4(codificador_4bits_2_out_12), .in_5(codificador_4bits_1_out_13), .in_6(codificador_4bits_2_out_13),
    .in_7(codificador_4bits_1_out_14), .in_8(codificador_4bits_2_out_14), .out_9(comparador_4bits_1_out_9));
  codificador_4bits codificador_4bits_3 (
    .in_1(in_25), .in_2(in_31), .in_3(in_37), .in_4(in_43), .in_5(in_49), .in_6(in_55), .in_7(in_57),
    .in_8(in_58), .in_9(in_59), .in_10(in_60), .out_11(codificador_4bits_3_out_11),
    .out_12(codificador_4bits_3_out_12), .out_13(codificador_4bits_3_out_13),
    .out_14(codificador_4bits_3_out_14));
  codificador_4bits codificador_4bits_4 (
    .in_1(in_62), .in_2(in_64), .in_3(in_66), .in_4(in_68), .in_5(in_73), .in_6(in_79), .in_7(in_85),
    .in_8(in_91), .in_9(in_97), .in_10(in_103), .out_11(codificador_4bits_4_out_11),
    .out_12(codificador_4bits_4_out_12), .out_13(codificador_4bits_4_out_13),
    .out_14(codificador_4bits_4_out_14));
  comparador_4bits comparador_4bits_2 (
    .in_1(codificador_4bits_3_out_11), .in_2(codificador_4bits_4_out_11), .in_3(codificador_4bits_3_out_12),
    .in_4(codificador_4bits_4_out_12), .in_5(codificador_4bits_3_out_13), .in_6(codificador_4bits_4_out_13),
    .in_7(codificador_4bits_3_out_14), .in_8(codificador_4bits_4_out_14), .out_9(comparador_4bits_2_out_9));
  codificador_4bits codificador_4bits_5 (
    .in_1(in_1), .in_2(in_6), .in_3(in_11), .in_4(in_16), .in_5(in_21), .in_6(in_27), .in_7(in_33),
    .in_8(in_39), .in_9(in_45), .in_10(in_51), .out_11(codificador_4bits_5_out_11),
    .out_12(codificador_4bits_5_out_12), .out_13(codificador_4bits_5_out_13),
    .out_14(codificador_4bits_5_out_14));
  codificador_4bits codificador_4bits_6 (
    .in_1(in_69), .in_2(in_75), .in_3(in_81), .in_4(in_87), .in_5(in_93), .in_6(in_99), .in_7(in_105),
    .in_8(in_109), .in_9(in_113), .in_10(in_117), .out_11(codificador_4bits_6_out_11),
    .out_12(codificador_4bits_6_out_12), .out_13(codificador_4bits_6_out_13),
    .out_14(codificador_4bits_6_out_14));
  comparador_4bits comparador_4bits_3 (
    .in_1(codificador_4bits_5_out_11), .in_2(codificador_4bits_6_out_11), .in_3(codificador_4bits_5_out_12),
    .in_4(codificador_4bits_6_out_12), .in_5(codificador_4bits_5_out_13), .in_6(codificador_4bits_6_out_13),
    .in_7(codificador_4bits_5_out_14), .in_8(codificador_4bits_6_out_14), .out_9(comparador_4bits_3_out_9));
  codificador_4bits codificador_4bits_7 (
    .in_1(in_5), .in_2(in_10), .in_3(in_15), .in_4(in_20), .in_5(in_26), .in_6(in_32), .in_7(in_38),
    .in_8(in_44), .in_9(in_50), .in_10(in_56), .out_11(codificador_4bits_7_out_11),
    .out_12(codificador_4bits_7_out_12), .out_13(codificador_4bits_7_out_13),
    .out_14(codificador_4bits_7_out_14));
  codificador_4bits codificador_4bits_8 (
    .in_1(in_74), .in_2(in_80), .in_3(in_86), .in_4(in_92), .in_5(in_98), .in_6(in_104), .in_7(in_108),
    .in_8(in_112), .in_9(in_116), .in_10(in_120), .out_11(codificador_4bits_8_out_11),
    .out_12(codificador_4bits_8_out_12), .out_13(codificador_4bits_8_out_13),
    .out_14(codificador_4bits_8_out_14));
  comparador_4bits comparador_4bits_4 (
    .in_1(codificador_4bits_7_out_11), .in_2(codificador_4bits_8_out_11), .in_3(codificador_4bits_7_out_12),
    .in_4(codificador_4bits_8_out_12), .in_5(codificador_4bits_7_out_13), .in_6(codificador_4bits_8_out_13),
    .in_7(codificador_4bits_7_out_14), .in_8(codificador_4bits_8_out_14), .out_9(comparador_4bits_4_out_9));
  codificador_4bits codificador_4bits_9 (
    .in_1(in_2), .in_2(in_7), .in_3(in_12), .in_4(in_17), .in_5(in_22), .in_6(in_28), .in_7(in_34),
    .in_8(in_40), .in_9(in_46), .in_10(in_52), .out_11(codificador_4bits_9_out_11),
    .out_12(codificador_4bits_9_out_12), .out_13(codificador_4bits_9_out_13),
    .out_14(codificador_4bits_9_out_14));
  codificador_4bits codificador_4bits_10 (
    .in_1(in_70), .in_2(in_76), .in_3(in_82), .in_4(in_88), .in_5(in_94), .in_6(in_100), .in_7(in_106),
    .in_8(in_110), .in_9(in_114), .in_10(in_118), .out_11(codificador_4bits_10_out_11),
    .out_12(codificador_4bits_10_out_12), .out_13(codificador_4bits_10_out_13),
    .out_14(codificador_4bits_10_out_14));
  comparador_4bits comparador_4bits_5 (
    .in_1(codificador_4bits_9_out_11), .in_2(codificador_4bits_10_out_11), .in_3(codificador_4bits_9_out_12),
    .in_4(codificador_4bits_10_out_12), .in_5(codificador_4bits_9_out_13),
    .in_6(codificador_4bits_10_out_13), .in_7(codificador_4bits_9_out_14),
    .in_8(codificador_4bits_10_out_14), .out_9(comparador_4bits_5_out_9));
  codificador_4bits codificador_4bits_11 (
    .in_1(in_3), .in_2(in_8), .in_3(in_13), .in_4(in_18), .in_5(in_23), .in_6(in_29), .in_7(in_35),
    .in_8(in_41), .in_9(in_47), .in_10(in_53), .out_11(codificador_4bits_11_out_11),
    .out_12(codificador_4bits_11_out_12), .out_13(codificador_4bits_11_out_13),
    .out_14(codificador_4bits_11_out_14));
  codificador_4bits codificador_4bits_12 (
    .in_1(in_71), .in_2(in_77), .in_3(in_83), .in_4(in_89), .in_5(in_95), .in_6(in_101), .in_7(in_107),
    .in_8(in_111), .in_9(in_115), .in_10(in_119), .out_11(codificador_4bits_12_out_11),
    .out_12(codificador_4bits_12_out_12), .out_13(codificador_4bits_12_out_13),
    .out_14(codificador_4bits_12_out_14));
  comparador_4bits comparador_4bits_6 (
    .in_1(codificador_4bits_11_out_11), .in_2(codificador_4bits_12_out_11),
    .in_3(codificador_4bits_11_out_12), .in_4(codificador_4bits_12_out_12),
    .in_5(codificador_4bits_11_out_13), .in_6(codificador_4bits_12_out_13),
    .in_7(codificador_4bits_11_out_14), .in_8(codificador_4bits_12_out_14), .out_9(comparador_4bits_6_out_9));
  and and_1 (and_1_out, comparador_4bits_6_out_9, comparador_4bits_5_out_9);
  and and_2 (and_2_out, comparador_4bits_4_out_9, comparador_4bits_3_out_9);
  and and_3 (and_3_out, comparador_4bits_2_out_9, comparador_4bits_1_out_9);
  and and_4 (and_4_out, and_1_out, and_2_out);
  and and_5 (out_121, and_4_out, and_3_out);
endmodule

module codificador_4bits (
  input  in_1,
  input  in_2,
  input  in_3,
  input  in_4,
  input  in_5,
  input  in_6,
  input  in_7,
  input  in_8,
  input  in_9,
  input  in_10,
  output out_11,
  output out_12,
  output out_13,
  output out_14
);

  wire or_1_out, or_2_out, or_3_out, or_4_out, or_5_out, or_6_out, or_7_out, or_11_out;

  or or_1 (or_1_out, in_6, in_5);
  or or_2 (or_2_out, in_4, in_3);
  or or_3 (or_3_out, in_8, in_7);
  or or_4 (or_4_out, in_4, in_3);
  or or_5 (or_5_out, in_9, in_7);
  or or_6 (or_6_out, in_5, in_3);
  or or_7 (or_7_out, in_1, in_1);
  or or_8 (out_11, in_2, in_1);
  or or_9 (out_12, or_1_out, or_2_out);
  or or_10 (out_13, or_3_out, or_4_out);
  or or_11 (or_11_out, or_5_out, or_6_out);
  or or_12 (out_14, or_11_out, or_7_out);
endmodule

module temporizador_3min (
  output out_1,
  output out_2,
  output out_3,
  output out_4,
  output out_5,
  output out_6,
  output out_7,
  output out_8,
  output out_9
);

  wire and_1_out, and_2_out, and_3_out, and_4_out, and_5_out, and_6_out, clock_1_out;

  Clock clock_1 (.out(clock_1_out));
  and and_1 (and_1_out, out_9, out_8, out_7);
  J_K_Flip_Flop #(.trigger("falling")) j_k_ff_1 (
    .J(and_1_out), .clk(clock_1_out), .K(and_1_out), .Q(out_6), .reset(and_3_out));  // open: Qn, preset, en
  and and_2 (and_2_out, out_9, out_8);
  J_K_Flip_Flop #(.trigger("falling")) j_k_ff_2 (
    .J(and_2_out), .clk(clock_1_out), .K(and_2_out), .Q(out_7), .reset(and_3_out));  // open: Qn, preset, en
  J_K_Flip_Flop #(.trigger("falling")) j_k_ff_3 (
    .J(out_9), .clk(clock_1_out), .K(out_9), .Q(out_8), .reset(and_3_out));  // open: Qn, preset, en
  and and_3 (and_3_out, out_6, out_8);
  J_K_Flip_Flop #(.trigger("falling")) j_k_ff_4 (
    .J(1'b1), .clk(clock_1_out), .K(1'b1), .Q(out_9), .reset(and_3_out));  // open: Qn, preset, en
  and and_4 (and_4_out, out_5, out_4);
  J_K_Flip_Flop #(.trigger("falling")) j_k_ff_5 (
    .J(and_4_out), .clk(and_3_out), .K(and_4_out), .Q(out_3), .reset(and_5_out));  // open: Qn, preset, en
  J_K_Flip_Flop #(.trigger("falling")) j_k_ff_6 (
    .J(out_5), .clk(and_3_out), .K(out_5), .Q(out_4), .reset(and_5_out));  // open: Qn, preset, en
  J_K_Flip_Flop #(.trigger("falling")) j_k_ff_7 (
    .J(1'b1), .clk(and_3_out), .K(1'b1), .Q(out_5), .reset(and_5_out));  // open: Qn, preset, en
  and and_5 (and_5_out, out_4, out_3);
  J_K_Flip_Flop #(.trigger("falling")) j_k_ff_8 (
    .J(out_2), .clk(and_5_out), .K(out_2), .Q(out_1), .reset(and_6_out));  // open: Qn, preset, en
  J_K_Flip_Flop #(.trigger("falling")) j_k_ff_9 (
    .J(1'b1), .clk(and_5_out), .K(1'b1), .Q(out_2), .reset(and_6_out));  // open: Qn, preset, en
  and and_6 (and_6_out, out_2, out_1);
endmodule

module contador_decadico (
  output out_1,
  output out_2,
  output out_3,
  output out_4
);

  wire and_1_out, and_2_out, clock_1_out, nand_1_out, not_1_out, not_2_out, not_3_out, not_4_out;

  and and_1 (and_1_out, out_4, out_3, out_2);
  Clock clock_1 (.out(clock_1_out));
  J_K_Flip_Flop #(.trigger("falling")) j_k_ff_1 (
    .J(and_1_out), .clk(clock_1_out), .K(and_1_out), .Q(out_1), .reset(not_1_out));  // open: Qn, preset, en
  not not_1 (not_1_out, nand_1_out);
  and and_2 (and_2_out, out_4, out_3);
  J_K_Flip_Flop #(.trigger("falling")) j_k_ff_2 (
    .J(and_2_out), .clk(clock_1_out), .K(and_2_out), .Q(out_2), .reset(not_2_out));  // open: Qn, preset, en
  not not_2 (not_2_out, nand_1_out);
  J_K_Flip_Flop #(.trigger("falling")) j_k_ff_3 (
    .J(out_4), .clk(clock_1_out), .K(out_4), .Q(out_3), .reset(not_3_out));  // open: Qn, preset, en
  not not_3 (not_3_out, nand_1_out);
  J_K_Flip_Flop #(.trigger("falling")) j_k_ff_4 (
    .J(1'b1), .clk(clock_1_out), .K(1'b1), .Q(out_4), .reset(not_4_out));  // open: Qn, preset, en
  not not_4 (not_4_out, nand_1_out);
  nand nand_1 (nand_1_out, out_1, out_3);
endmodule
